# Fritzing sketch light_intensity (saved by Fritzing 0.9.3b)

parts:
  A_O = LM 358 Dual Op-Amp [package="SO 08 [SMD]"]
  R1 = Resistor [tolerance=±5% resistance=10k package="2010 [SMD]"]
  P1 = S1133 Si Photodiode [package="8mm Ceramic [THT]"]
  MCU = ESP32-38PinWide [part_number=ESP32-38PinWide]

nets:
  N1: A_O.connector0, R1.Pin_1, MCU.GPIO35
  N2: A_O.connector1, R1.Pin_0, P1.anode
  N3: A_O.connector2, A_O.connector3, P1.cathode, MCU.GND
  N4: A_O.connector7, MCU.3.3

custom parts:
  ESP32-38PinWide: Generic 38-Pin ESP32 with wide format (only access to one side of pins on a breadboard) based on Stephen Lilley's HiLetgo ESP-WROOM-32 ESP32 ESP-32S Development Board.
