# Fritzing sketch pir (saved by Fritzing 0.9.3b)

parts:
  Componente1 = HC-SR501 Body Sensor Module
  MCU1 = ESP-WROOM-32 [ESP-32S] Module [part_number=ESP-WROOM-32]

nets:
  N1: Componente1.VCC, MCU1.Pin_2
  N2: Componente1.OUT, MCU1.Pin_10
  N3: Componente1.GND, MCU1.Pin_1, MCU1.Pin_15

custom parts:
  HC-SR501 Body Sensor Module: Pyroelectric Infrared PIR Motion Sensor Detector Module
  ESP-WROOM-32 [ESP-32S] Module: Espressif ESP-WROOM-32 WiFi/Bluetooth LE microcontroller module also known as the Ai-Thinker ESP-32S module with similar formfactor. The ESP32 is a microcontroller chip with WiFi and BLE capabilities. The chip is developed by Espressif and is the successor to the popular ESP8266 WiFi module.
